# Fritzing sketch Untitled Sketch 2 (saved by Fritzing 0.9.4)

parts:
  U1 = attiny85 [package=dip]
  U2 = 74HC595 [package="DIP16 [THT]"]
  Компонент1 = Arduino Uno (Rev3)
  R5 = Resistor [tolerance=±1% resistance=4.3M package=THT]
  R3 = Resistor [tolerance=±5% resistance=7.5k package=THT]
  R1 = Resistor [tolerance=±5% resistance=7.5k package=THT]
  R7 = Resistor [tolerance=±5% resistance=7.5k package=THT]
  R4 = Resistor [tolerance=±1% resistance=4.3M package=THT]
  R2 = Resistor [tolerance=±1% resistance=4.3M package=THT]
  R8 = Resistor [tolerance=±1% resistance=4.3M package=THT]
  R6 = Resistor [tolerance=±5% resistance=7.5k package=THT]

nets:
  GND: U1.Pin_4, U2.GND, U2.OE, Компонент1.GND, R7.Pin_1
  N1: U1.Pin_5, U2.DS
  N2: U1.Pin_6, U2.SH_CP
  N3: U1.Pin_7, U2.ST_CP
  VCC: U1.Pin_8, U2.MR, U2.VCC, Компонент1.5V
  N4: U2.Q1, R5.Pin_1
  N5: U2.Q2, R4.Pin_1
  N6: U2.Q3, R2.Pin_1
  N7: U2.Q0, R8.Pin_1
  N8: R5.Pin_0, R3.Pin_1, R6.Pin_0
  N9: R3.Pin_0, R1.Pin_1, R4.Pin_0
  N10: R1.Pin_0, R2.Pin_0
  N11: R7.Pin_0, R8.Pin_0, R6.Pin_1
